# Fritzing sketch lectogram (saved by Fritzing 0.9.3b)

parts:
  DFPlayer_Mini1 = DFPlayer MINI [package="DIP (Dual Inline) [THT]"]
  SP1 = SPEAKER [package=pcb_mount_speaker]
  R4 = Resistor [tolerance=±5% resistance=1k package="2010 [SMD]"]
  R2 = Resistor [tolerance=±5% resistance=220 package="2010 [SMD]"]
  U5 = Mini-360 DC-DC Buck converter [package=THT]
  U6 = LIPO-1000mAh [package=lipo-1000]
  Part3 = RFID-RC522-v2
  Componente1 = Arduino Nano (Rev3.0) (ICSP)
  Componente2 = USB LiPoly Charger  # not connected
  Componente3 = 24 NeoPixel Ring [part_number=1586]

nets:
  N1: DFPlayer_Mini1.VCC, U5.IN+, U6.+
  N2: DFPlayer_Mini1.RX, R4.Pin_0, R2.Pin_0
  N3: DFPlayer_Mini1.TX, Componente1.D2
  N4: DFPlayer_Mini1.SPK1, SP1.-
  GND: DFPlayer_Mini1.GND, U5.OUT-, Part3.MOSI, Componente1.GND, Componente3.GND
  N5: DFPlayer_Mini1.SPK2, SP1.+
  N6: R4.Pin_1, Componente1.D3
  N7: U5.IN-, U6.-
  N8: U5.OUT+, Componente1.VIN
  N9: Part3.SDA, Componente1.3V3
  N10: Part3.SCK, Componente1.D9
  N11: Part3.IRQ, Componente1.D12/MISO
  N12: Part3.GND, Componente1.D11/MOSI
  N13: Part3.RST, Componente1.D13/SCK
  N14: Part3.3.3V, Componente1.D10
  N15: Componente1.D8, Componente3.IN
  5V: Componente1.5V, Componente3.VDD

notes:
  Tarjeta o llavero 1
  Tarjeta o llavero 2
  Tarjeta o llavero 3

custom parts:
  DFPlayer MINI: MP3 module by DFRobot.com for playing Music from an SD-Card. Supports WAV and MP3 files.
  Mini-360 DC-DC Buck converter: Mini-360 DC-DC Buck converter. Tiny buck step down voltage converter, input voltage 4.75 to 23V output 1 to 17V adjustable. Available from ebay and the like.
  RFID-RC522-v2: A simple China made RFID-RC522 Reader; do check the pin labels, as this is a MFRC522 based clone.
  24 NeoPixel Ring: 24 ultra bright smart LED NeoPixels are arranged in a circle with 2.6" (66mm) outer diameter. The rings are 'chainable' - connect the output pin of one to the input pin of another. Use only one microcontroller pin to control as many as you can chain together! Each LED is addressable as the driver chip is inside the LED. Each one has ~18mA constant current drive so the color will be very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
